# Fritzing sketch circuit (saved by Fritzing 0.9.4)
breadboards: 1

parts:
  Part1 = Arduino Uno (Rev3)
  U1 = Module 4 Relais 5V [package="Module 4 Relais 5V"]
  LED1 = LED - 3mm [color="Green (555nm)" package="3 mm [THT]"]
  LED2 = LED - 3mm [color="Red (633nm)" package="3 mm [THT]"]
  J1 = Piezo Speaker
  Part2 = LCD1602-I2C
  M1 = E18-D80NK_1 [package=THT]
  M2 = E18-D80NK_1 [package=THT]
  JACK1 = 2.1mm Barrel Jack with Terminal Block
  JACK2 = 2.1mm Barrel Jack with Terminal Block

nets:
  N1: Part1.D9_PWM, J1.pin2
  N2: Part1.A4/SDA, Part2.SDA
  N3: Part1.A5/SCL, Part2.SCL
  N4: Part1.D2, M1.pin3
  N5: Part1.D3_PWM, M2.pin3
  N6: Part1.D6_PWM, U1.IN1
  N7: Part1.D7, U1.IN2
  VCC: Part1.5V, U1.VCC, Part2.VCC, M1.pin2, M2.pin2
  GND: Part1.GND, U1.GND, J1.pin1, Part2.GND, M1.pin1, M2.pin1
  N8: U1.K1-NF, U1.K2-NF, JACK1.POS, JACK2.POS
  N9: U1.K1-NO, LED1.cathode
  N10: U1.K2-NO, LED2.cathode
  N11: LED2.anode, JACK1.NEG, JACK2.NEG

custom parts:
  Module 4 Relais 5V: Module 4 Relais 5V 4x SPD-06VDC-SD-C
  LCD1602-I2C: A standard character display, usually with 2x16 characters. Comes in many colors with LCM1602 IIC attached.
  E18-D80NK_1: E18-D80NK Proximity Sensor module.
